# Fritzing sketch schematic (saved by Fritzing 0.9.2b)
breadboards: 1

parts:
  WeMos_D1_Mini1 = WeMos D1 Mini
  DHT1 = DHT22 Humidity and Temperature Sensor
  R1 = Resistor [tolerance=±5% resistance=220 package="2512 [SMD]"]
  U3 = MAX7219 [package=dil24]
  LED1 = smd LED [color="Red (633nm)" package="0603 [SMD]"]

nets:
  5V: WeMos_D1_Mini1.5V, DHT1.VDD, U3.VCC
  N1: WeMos_D1_Mini1.D1, DHT1.DATA
  N2: WeMos_D1_Mini1.D2, U3.DIN
  N3: WeMos_D1_Mini1.D3, U3.CS
  N4: WeMos_D1_Mini1.D4, U3.CLK
  N5: WeMos_D1_Mini1.D5, R1.Pin_0
  GND: WeMos_D1_Mini1.G, DHT1.GND, U3.GND, LED1.cathode
  N6: R1.Pin_1, LED1.anode

custom parts:
  WeMos D1 Mini: The D1 mini is a mini wifi board based on ESP-8266EX.
  MAX7219: 8-digit, 8-segment LED display driver, serial input
